// Logisim project 16bit_Computer.circ as structural Verilog: 17 circuits, main circuit main
module main (
);

  wire and_1_out, and_2_out, CLK, DT_EN, interupt_request_1_int, interupt_request_1_nmi, IO, IO_1, IO_2,
       IRQ_1, K2, K4, K16, K32, pull_resistor_1_node, RAMCONT, Reset;
  wire [6:0] keyboard_1_data;
  wire [15:0] ADDR, ADDRM, Data;
  wire [15:7] pull_resistor_2_node;

  RAM_2k ram_2k_1 (
    .Write(RAMCONT), .DT_EN(DT_EN), .ADDR(ADDRM), .IO_EN(IO), .CLK(CLK), .EN(K2), .Data_IN(Data),
    .Data_Out(Data));
  RAM_32k ram_32k_1 (
    .Write(RAMCONT), .DT_EN(DT_EN), .ADDR(ADDRM), .IO_EN(IO), .CLK(CLK), .EN(K32), .Data_IN(Data),
    .Data_Out(Data));
  and and_1 (and_1_out, K16, ~IO);  // AND_Gate
  MMAP mmap_1 (.ADDR(ADDR), .EN_1(K16), .EN_2(K32), .EN_3(K2), .EN_4(K4), .ADDR_OUT(ADDRM));
  ROM_16k rom_16k_1 (.ADDR(ADDRM), .OUT_EN(and_1_out), .Data_Out(Data));
  Interupt_Request interupt_request_1 (
    .IRQ_1(IRQ_1), .Clock(CLK), .INT(interupt_request_1_int), .NMI(interupt_request_1_nmi));  // open: IRQ_4, IRQ_3, IRQ_2
  IO_interface io_interface_1 (.IO_EN(IO), .ADDR(ADDR), .P_2(IO_2), .P_1(IO_1));  // open: P_3, P_4
  CPUz16 cpuz16_1 (
    .NMI(interupt_request_1_nmi), .INT(interupt_request_1_int), .Clock(CLK), .Reset(Reset), .Data_IN(Data),
    .Byte_Enable(DT_EN), .ADDR(ADDR), .Data_Out(Data), .IO(IO), .Ram_Control(RAMCONT));
  and and_2 (and_2_out, K4, ~IO);  // AND_Gate
  Clock clock_1 (.out(CLK));
  ROM_4k rom_4k_1 (.ADDR(ADDRM), .OUT_EN(and_2_out), .Data_Out(Data));
  TTY #(.cols(64), .rows(32)) tty_1 (.data(Data[6:0]), .clk(CLK), .we(pull_resistor_1_node), .clr(Reset));
  Pull_Resistor pull_resistor_1 (.node(pull_resistor_1_node));
  assign pull_resistor_1_node = IO_1 ? RAMCONT : 1'bz;  // Controlled_Buffer controlled_buffer_1
  Keyboard #(.trigger("falling")) keyboard_1 (.clk(CLK), .re(IO_2), .clr(Reset), .avail(IRQ_1), .data(keyboard_1_data));
  Pull_Resistor pull_resistor_2 (.node({pull_resistor_2_node, keyboard_1_data}));
  assign Data = IO_2 ? {pull_resistor_2_node, keyboard_1_data} : 16'bz;  // Controlled_Buffer controlled_buffer_2
  Button button_1 (.out(Reset));
endmodule

module CPUz16 (
  input  Clock,
  input  Reset,
  input  [15:0] Data_IN,
  input  NMI,
  input  INT,
  output [15:0] ADDR,
  output [15:0] Data_Out,
  output IO,
  output Ram_Control,
  output Byte_Enable
);

  wire ALU_EN, control_1_b_en, control_1_wr_en, MOV, RD, Write_EN;
  wire [4:0] ALU_OP;
  wire [7:0] alu_1_com_flags, control_1_byte, controlled_buffer_1_out, Flag;
  wire [15:0] alu_1_alu_output, control_1_addr_access, controlled_buffer_2_out, register_file_1_a_out,
       register_file_1_b_out;

  assign controlled_buffer_1_out = Byte_Enable ? Data_IN[15:8] : 8'bz;  // Controlled_Buffer controlled_buffer_1
  Control control_1 (
    .Pointer(register_file_1_a_out), .Clock(Clock), .Reset(Reset), .NMI(NMI), .INT(INT), .Flags(Flag),
    .Data_IN(Data_IN), .ADDR_Access(control_1_addr_access), .B_EN(control_1_b_en), .Byte(control_1_byte),
    .CALL_DATA(Data_Out), .CALL_RET(control_1_addr_access), .ALU_Enable(ALU_EN), .ALU_opCode(ALU_OP),
    .REG_Write(Write_EN), .Data_BusEN(RD), .RG_RGMOV(MOV), .RAM_Write(Ram_Control), .WR_EN(control_1_wr_en),
    .IO(IO), .Data_Type(Byte_Enable));
  Pull_Resistor pull_resistor_1 (.node(controlled_buffer_1_out));
  Multiplexer #(.width(16)) multiplexer_1 (
    .in0(control_1_addr_access), .in1(register_file_1_b_out), .out(ADDR), .sel(control_1_b_en));
  assign controlled_buffer_2_out = RD ? {controlled_buffer_1_out, Data_IN[7:0]} : 16'bz;  // Controlled_Buffer controlled_buffer_2
  assign controlled_buffer_2_out = ALU_EN ? alu_1_alu_output : 16'bz;  // Controlled_Buffer controlled_buffer_3
  assign controlled_buffer_2_out = MOV ? register_file_1_a_out : 16'bz;  // Controlled_Buffer controlled_buffer_4
  Register_File register_file_1 (
    .Reset(Reset), .Write_Select(control_1_byte[3:0]), .Clock(Clock), .Write(control_1_byte[5:4]),
    .Write_EN(Write_EN), .WRITE_IN(controlled_buffer_2_out), .A_OUT(register_file_1_a_out),
    .B_OUT(register_file_1_b_out));
  assign Data_Out = control_1_wr_en ? register_file_1_a_out : 16'bz;  // Controlled_Buffer controlled_buffer_5
  ALU alu_1 (
    .OPcode(ALU_OP), .Input_A(register_file_1_a_out), .Input_B(register_file_1_b_out),
    .COM_Flags(alu_1_com_flags[5:0]), .ALU_Output(alu_1_alu_output), .Overflow_Flag(alu_1_com_flags[7]),
    .Negative_Flag(alu_1_com_flags[6]));
  Flags_RG flags_rg_1 (.Reset(Reset), .Flag_Input(alu_1_com_flags), .Write_EN(ALU_EN), .Clock(Clock), .Result(Flag));

  // Other names for the same wires on the sheet: CLK = Clock; RST = Reset
endmodule

module ALU (
  input  [15:0] Input_A,
  input  [15:0] Input_B,
  input  [4:0] OPcode,
  output Overflow_Flag,
  output Negative_Flag,
  output [15:0] ALU_Output,
  output [5:0] COM_Flags
);

  wire and_2_out, and_3_out;
  wire [5:0] not_2_out, not_3_out;
  wire [15:0] adder_1_out, adder_2_out, and_1_out, divider_1_out, divider_1_rem, divider_2_out,
       divider_2_rem, multiplier_1_out, multiplier_2_out, negator_1_out, not_1_out, or_1_out, shifter_1_out,
       shifter_2_out, shifter_3_out, shifter_4_out, shifter_5_out, subtractor_1_out, subtractor_2_out,
       xor_1_out;

  Adder #(.width(16)) adder_1 (.a(Input_A), .b(Input_B), .out(adder_1_out), .cout(Overflow_Flag));  // open: cin
  Subtractor #(.width(16)) subtractor_1 (.a(Input_A), .b(Input_B), .out(subtractor_1_out));  // open: bin, bout
  Multiplier #(.width(16)) multiplier_1 (.a(Input_A), .b(Input_B), .out(multiplier_1_out));  // open: cin, cout
  Divider #(.width(16)) divider_1 (.a(Input_A), .b(Input_B), .out(divider_1_out), .rem(divider_1_rem));  // open: upper
  assign and_1_out = Input_A & Input_B;  // AND_Gate and_1, 16 bits wide
  assign or_1_out = Input_A | Input_B;  // OR_Gate or_1, 16 bits wide
  assign not_1_out = ~Input_A;  // NOT_Gate not_1, 16 bits wide
  assign xor_1_out = Input_A ^ Input_B;  // XOR_Gate xor_1, 16 bits wide
  Negator #(.width(16)) negator_1 (.in(Input_A), .out(negator_1_out));
  or or_2 (not_2_out[2], not_2_out[5], not_2_out[4]);
  Comparator #(.width(16)) comparator_1 (
    .a(Input_A), .b(Input_B), .gt(not_2_out[5]), .eq(not_2_out[4]), .lt(not_2_out[3]));
  or or_3 (not_2_out[1], not_2_out[4], not_2_out[3]);
  or or_4 (not_3_out[2], not_3_out[5], not_3_out[4]);
  Comparator #(.mode("unsigned"), .width(16)) comparator_2 (
    .a(Input_A), .b(Input_B), .gt(not_3_out[5]), .eq(not_3_out[4]), .lt(not_3_out[3]));
  or or_5 (not_3_out[1], not_3_out[4], not_3_out[3]);
  Shifter #(.width(16)) shifter_1 (.in(Input_A), .\dist (Input_B[3:0]), .out(shifter_1_out));
  Shifter #(.shift("lr"), .width(16)) shifter_2 (.in(Input_A), .\dist (Input_B[3:0]), .out(shifter_2_out));
  Shifter #(.shift("ar"), .width(16)) shifter_3 (.in(Input_A), .\dist (Input_B[3:0]), .out(shifter_3_out));
  Shifter #(.shift("rl"), .width(16)) shifter_4 (.in(Input_A), .\dist (Input_B[3:0]), .out(shifter_4_out));
  Shifter #(.shift("rr"), .width(16)) shifter_5 (.in(Input_A), .\dist (Input_B[3:0]), .out(shifter_5_out));
  Adder #(.width(16)) adder_2 (.a(Input_A), .b(16'h1), .out(adder_2_out));  // open: cin, cout
  Subtractor #(.width(16)) subtractor_2 (.a(Input_A), .b(16'h1), .out(subtractor_2_out));  // open: bin, bout
  Multiplier #(.mode("twosComplement"), .width(16)) multiplier_2 (
    .a(Input_A), .b(Input_B), .out(multiplier_2_out));  // open: cin, cout
  Divider #(.mode("twosComplement"), .width(16)) divider_2 (
    .a(Input_A), .b(Input_B), .out(divider_2_out), .rem(divider_2_rem));  // open: upper
  not not_2 (not_2_out[0], not_2_out[4]);
  not not_3 (not_3_out[0], not_3_out[4]);
  and and_2 (and_2_out, OPcode[0], OPcode[1], ~OPcode[2], ~OPcode[3], OPcode[4]);  // AND_Gate
  and and_3 (and_3_out, ~OPcode[0], ~OPcode[1], OPcode[2], ~OPcode[3], OPcode[4]);  // AND_Gate
  assign COM_Flags = and_2_out ? not_2_out : 6'bz;  // Controlled_Buffer controlled_buffer_1
  assign COM_Flags = and_3_out ? not_3_out : 6'bz;  // Controlled_Buffer controlled_buffer_2
  Pull_Resistor pull_resistor_1 (.node(ALU_Output));
  Multiplexer #(.select(5), .width(16)) multiplexer_1 (
    .in0(adder_1_out), .in1(subtractor_1_out), .in2(multiplier_1_out), .in3(divider_1_out), .in4(and_1_out),
    .in5(or_1_out), .in6(xor_1_out), .in7(negator_1_out), .in8(not_1_out), .in9(divider_1_rem),
    .in10(shifter_1_out), .in11(shifter_2_out), .in12(shifter_3_out), .in13(shifter_4_out),
    .in14(shifter_5_out), .in15(adder_2_out), .in16(subtractor_2_out), .in17(multiplier_2_out),
    .in18(divider_2_out), .in21(divider_2_rem), .out(ALU_Output), .sel(OPcode));  // open: in19, in20, in22, in23, in24, in25, in26, in27, in28, in29, in30, in31

  assign Negative_Flag = ALU_Output[15];
endmodule

module Register_File (
  input  [15:0] WRITE_IN,
  input  [3:0] Write_Select,
  input  Clock,
  input  [1:0] Write,
  input  Write_EN,
  input  Reset,
  output [15:0] A_OUT,
  output [15:0] B_OUT
);

  wire decoder_1_out0, decoder_1_out1, decoder_1_out2, decoder_1_out3;
  wire [15:0] AH_q, BH_q, CH_q, DH_q;

  Decoder #(.select(2)) decoder_1 (
    .out0(decoder_1_out0), .out1(decoder_1_out1), .out2(decoder_1_out2), .out3(decoder_1_out3), .sel(Write),
    .en(Write_EN));
  Register #(.trigger("falling"), .width(16)) AH (
    .D(WRITE_IN), .en(decoder_1_out0), .clk(Clock), .Q(AH_q), .clr(Reset));
  Register #(.trigger("falling"), .width(16)) BH (
    .D(WRITE_IN), .en(decoder_1_out1), .clk(Clock), .Q(BH_q), .clr(Reset));
  Register #(.trigger("falling"), .width(16)) CH (
    .D(WRITE_IN), .en(decoder_1_out2), .clk(Clock), .Q(CH_q), .clr(Reset));
  Register #(.trigger("falling"), .width(16)) DH (
    .D(WRITE_IN), .en(decoder_1_out3), .clk(Clock), .Q(DH_q), .clr(Reset));
  Multiplexer #(.select(2), .width(16)) multiplexer_1 (
    .in0(AH_q), .in1(BH_q), .in2(CH_q), .in3(DH_q), .out(A_OUT), .sel(Write_Select[1:0]));
  Multiplexer #(.select(2), .width(16)) multiplexer_2 (
    .in0(AH_q), .in1(BH_q), .in2(CH_q), .in3(DH_q), .out(B_OUT), .sel(Write_Select[3:2]));
endmodule

module Flags_RG (
  input  [7:0] Flag_Input,
  input  Write_EN,
  input  Clock,
  input  Reset,
  output [7:0] Result
);

  Register register_1 (.D(Flag_Input), .en(Write_EN), .clk(Clock), .Q(Result), .clr(Reset));
  Pull_Resistor pull_resistor_1 (.node(Flag_Input));
  LED led_1 (.in(Result[7]));
  LED led_2 (.in(Result[6]));
  LED led_3 (.in(Result[5]));
  LED led_4 (.in(Result[4]));
  LED led_5 (.in(Result[3]));
  LED led_6 (.in(Result[2]));
  LED led_7 (.in(Result[1]));
  LED led_8 (.in(Result[0]));
endmodule

module Control (
  input  [15:0] Data_IN,
  input  Clock,
  input  Reset,
  input  [15:0] Pointer,
  input  [7:0] Flags,
  input  NMI,
  input  INT,
  output [7:0] Byte,
  output [15:0] ADDR_Access,
  output [15:0] CALL_DATA,
  output [15:0] CALL_RET,
  output [4:0] ALU_opCode,
  output Data_Type,
  output ALU_Enable,
  output IO,
  output REG_Write,
  output B_EN,
  output Data_BusEN,
  output RG_RGMOV,
  output RAM_Write,
  output WR_EN
);

  wire ADD, and_1_out, and_2_out, and_3_out, and_5_out, and_6_out, and_7_out, Byte_Enable, CALL, Call_EN,
       CHGEN, CLR, COM, controlled_buffer_9_out, controlled_buffer_21_out, controlled_buffer_44_out,
       Count_Enable, cycle4timer_1_s3, cycle4timer_2_s1, cycle4timer_2_s2, cycle4timer_2_s3,
       cycle4timer_3_s1, cycle4timer_3_s2, cycle4timer_3_s3, cycle4timer_4_s3, cycle4timer_5_s2,
       cycle4timer_6_s1, cycle4timer_6_s3, d_ff_2_qn, DEC, decoder_1_out0, decoder_1_out1, decoder_2_out2,
       decoder_2_out3, decoder_2_out4, decoder_2_out5, decoder_3_out9, decoder_3_out10, decoder_3_out11,
       decoder_3_out12, decoder_3_out13, decoder_3_out14, decoder_3_out16, decoder_3_out17, DIV, FSHEN, FSHI,
       HLT, INC, INp, INT_EN, INT_t, JMP, Jmp_t, JMPrst, JpE, JpI, JpL, JPLD, JpLE, JpM, JpME, JpN, JpNO,
       JpO, LAND, LDIH, LDSB, LDSP, LNOT, LOR, LXOR, MUL, NEG, nor_1_out, nor_2_out, nor_3_out, not_2_out,
       or_1_out, or_2_out, or_4_out, or_6_out, or_7_out, or_8_out, or_9_out, or_12_out, or_13_out, or_16_out,
       or_17_out, or_19_out, or_20_out, or_21_out, or_22_out, or_27_out, or_30_out, or_31_out, or_32_out,
       OUTp, PC_R, PC_WR, POP, pull_resistor_1_node, pull_resistor_2_node, pull_resistor_3_node,
       pull_resistor_6_node, pull_resistor_7_node, pull_resistor_8_node, pull_resistor_9_node,
       pull_resistor_13_node, PUSH, PUSHorPULL, RD, RDP, RDPG, RDWR1, RDWR2, RET, RETA, ROTL, ROTR, RSTINST,
       s_r_ff_1_q, SBEN, SCOM, SDIV, Set, SFTA, SFTL, SFTR, SMUL, SREM, SUB, TRAM, UREM, WR, WR_EN_t, WRP;
  wire [15:0] Call_ADDR, controlled_buffer_12_out, DT, Interupt_Handler_q, PC, Saved_Addr_q, SavedINT,
       Stack_Addr;
  wire [15:8] INST_q;

  or or_1 (or_1_out, PUSHorPULL, Call_EN);
  or or_2 (or_2_out, PUSH, CALL);
  Stack_Pack stack_pack_1 (
    .Reset(Reset), .Stack_Enable(or_1_out), .Push(or_2_out), .DataType(SBEN), .Pointer(Pointer),
    .LD_Stack(LDSP), .LD_Base(LDSB), .Clock(Clock), .Stack_Addr(Stack_Addr));
  or or_3 (Count_Enable, or_16_out, or_12_out, or_8_out, or_6_out, RDWR1);
  Cycle4Timer cycle4timer_1 (
    .EN(or_4_out), .CLK(Clock), .RST(Reset), .S1(RDWR1), .S2(WR_EN_t), .S3(cycle4timer_1_s3));  // open: S0
  or or_4 (or_4_out, RD, OUTp, INp, WR);
  S_R_Flip_Flop #(.trigger("falling")) s_r_ff_1 (
    .clk(Clock), .Q(s_r_ff_1_q), .reset(or_7_out), .preset(NMI));  // open: S, R, Qn
  S_R_Flip_Flop #(.trigger("falling")) s_r_ff_2 (
    .S(1'b0), .R(pull_resistor_1_node), .clk(Clock), .Q(INT_t), .reset(or_7_out), .preset(INT));  // open: Qn
  Pull_Resistor pull_resistor_1 (.node(pull_resistor_1_node));
  assign pull_resistor_1_node = INT_t ? 1'b1 : 1'bz;  // Controlled_Buffer controlled_buffer_1
  or or_5 (PUSHorPULL, cycle4timer_2_s2, cycle4timer_3_s2);
  or or_6 (or_6_out, cycle4timer_2_s1, cycle4timer_2_s2);
  Cycle4Timer cycle4timer_2 (
    .EN(PUSH), .CLK(Clock), .RST(Reset), .S1(cycle4timer_2_s1), .S2(cycle4timer_2_s2), .S3(cycle4timer_2_s3));  // open: S0
  Register #(.trigger("low"), .width(1)) register_1 (.D(Byte_Enable), .en(Set), .clk(Clock), .Q(SBEN), .clr(Reset));
  or or_7 (or_7_out, JMPrst, Reset);
  or or_8 (or_8_out, cycle4timer_3_s1, cycle4timer_3_s2);
  Cycle4Timer cycle4timer_3 (
    .EN(POP), .CLK(Clock), .RST(Reset), .S1(cycle4timer_3_s1), .S2(cycle4timer_3_s2), .S3(cycle4timer_3_s3));  // open: S0
  or or_9 (or_9_out, PC_R, cycle4timer_5_s2);
  or or_10 (INT_EN, INT_t, JpI);
  and and_1 (and_1_out, ~INT_EN, JMP);  // AND_Gate
  Branch branch_1 (
    .Flags(Flags), .NMI(s_r_ff_1_q), .INT(INT_t), .Jump(Jmp_t), .Jump_Less(JpL), .Jump_Equal(JpE),
    .Jump_More(JpM), .Jump_Overflow(JpO), .Jump_Negative(JpN), .Jump_MoreEqu(JpME), .Jump_LessEqu(JpLE),
    .Jump_Not(JpNO), .Jump_Int(JpI), .Jump_Enable(JMP));
  or or_11 (Call_EN, PC_R, cycle4timer_6_s1);
  or or_12 (or_12_out, RDWR2, PC_R);
  Cycle4Timer cycle4timer_4 (
    .EN(CALL), .CLK(Clock), .RST(Reset), .S1(RDWR2), .S2(PC_R), .S3(cycle4timer_4_s3));  // open: S0
  not not_1 (Data_Type, SBEN);
  LED u_Byte_Enable (.in(Data_Type));
  assign DT = or_9_out ? PC : 16'bz;  // Controlled_Buffer controlled_buffer_2
  and and_2 (and_2_out, ~or_13_out, ~Count_Enable);  // AND_Gate
  or or_13 (or_13_out, JPLD, cycle4timer_5_s2, JMPrst);
  Cycle4Timer cycle4timer_5 (
    .EN(and_1_out), .CLK(Clock), .RST(Reset), .S1(JPLD), .S2(cycle4timer_5_s2), .S3(JMPrst));  // open: S0
  D_Flip_Flop #(.trigger("falling")) d_ff_1 (
    .D(1'b0), .clk(FSHI), .Q(FSHEN), .preset(INT_t), .reset(Reset));  // open: Qn
  or or_14 (CHGEN, RD, WR, JMP, POP, PUSH, OUTp, INp, CALL, RET);
  or or_15 (PC_WR, PC_R, RETA);
  or or_16 (or_16_out, cycle4timer_6_s1, RETA);
  Pull_Resistor pull_resistor_2 (.node(pull_resistor_2_node));
  nor nor_1 (nor_1_out, pull_resistor_2_node, INT_EN);
  Pull_Resistor pull_resistor_3 (.node(pull_resistor_3_node));
  assign pull_resistor_3_node = nor_1_out ? and_2_out : 1'bz;  // Controlled_Buffer controlled_buffer_3
  assign DT = pull_resistor_3_node ? Call_ADDR : 16'bz;  // Controlled_Buffer controlled_buffer_4
  Register #(.trigger("falling"), .width(16)) u_PC (.D(DT), .en(or_17_out), .clk(Clock), .Q(SavedINT), .clr(Reset));
  or or_17 (or_17_out, and_2_out, cycle4timer_5_s2, PC_WR);
  Cycle4Timer cycle4timer_6 (
    .EN(RET), .CLK(Clock), .RST(Reset), .S1(cycle4timer_6_s1), .S2(RETA), .S3(cycle4timer_6_s3));  // open: S0
  assign pull_resistor_2_node = FSHEN ? FSHI : 1'bz;  // Controlled_Buffer controlled_buffer_5
  or or_18 (RSTINST, JMPrst, cycle4timer_1_s3, cycle4timer_2_s3, cycle4timer_3_s3, cycle4timer_4_s3, cycle4timer_6_s3);
  assign DT = RETA ? Data_IN : 16'bz;  // Controlled_Buffer controlled_buffer_6
  Adder #(.width(16)) adder_1 (.a(SavedINT), .b(16'h2), .out(Call_ADDR));  // open: cin, cout
  not not_2 (not_2_out, CHGEN);
  or or_19 (or_19_out, RDWR1, RDWR2, JPLD);
  assign ADDR_Access = WR_EN_t ? PC : 16'bz;  // Controlled_Buffer controlled_buffer_7
  Pull_Resistor pull_resistor_4 (.node(ADDR_Access));
  assign ADDR_Access = nor_2_out ? SavedINT : 16'bz;  // Controlled_Buffer controlled_buffer_8
  nor nor_2 (nor_2_out, WR_EN_t, or_20_out);
  or or_20 (or_20_out, PUSHorPULL, PC_WR);
  Register #(.width(16)) INST (
    .D(Data_IN), .en(controlled_buffer_9_out), .clk(and_3_out), .Q({INST_q, Byte}), .clr(or_21_out));
  assign controlled_buffer_9_out = not_2_out ? 1'b1 : 1'bz;  // Controlled_Buffer controlled_buffer_9
  Pull_Resistor pull_resistor_5 (.node(controlled_buffer_9_out));
  and and_3 (and_3_out, Clock, ~or_21_out);  // AND_Gate
  Register #(.width(16)) ADDR (.D(Data_IN), .en(pull_resistor_6_node), .clk(Clock), .Q(PC), .clr(or_21_out));
  Pull_Resistor pull_resistor_6 (.node(pull_resistor_6_node));
  assign pull_resistor_6_node = CHGEN ? or_19_out : 1'bz;  // Controlled_Buffer controlled_buffer_10
  or or_21 (or_21_out, Reset, RSTINST);
  assign ADDR_Access = or_20_out ? Stack_Addr : 16'bz;  // Controlled_Buffer controlled_buffer_11
  D_Flip_Flop #(.trigger("falling")) d_ff_2 (
    .D(INT_EN), .clk(Clock), .Qn(d_ff_2_qn), .reset(Reset));  // open: Q, preset
  assign controlled_buffer_12_out = RDWR2 ? Call_ADDR : 16'bz;  // Controlled_Buffer controlled_buffer_12
  assign controlled_buffer_12_out = pull_resistor_7_node ? SavedINT : 16'bz;  // Controlled_Buffer controlled_buffer_13
  or or_22 (or_22_out, RDWR2, pull_resistor_7_node);
  Pull_Resistor pull_resistor_7 (.node(pull_resistor_7_node));
  assign pull_resistor_7_node = d_ff_2_qn ? INT_EN : 1'bz;  // Controlled_Buffer controlled_buffer_14
  Register #(.width(16)) Interupt_Handler (.D(Pointer), .en(LDIH), .clk(Clock), .Q(Interupt_Handler_q), .clr(Reset));
  Register #(.trigger("high"), .width(16)) Saved_Addr (
    .D(controlled_buffer_12_out), .en(or_22_out), .clk(Clock), .Q(Saved_Addr_q), .clr(Reset));
  or or_23 (B_EN, RDP, WRP);
  assign DT = INT_EN ? Interupt_Handler_q : 16'bz;  // Controlled_Buffer controlled_buffer_15
  assign DT = pull_resistor_8_node ? Saved_Addr_q : 16'bz;  // Controlled_Buffer controlled_buffer_16
  Pull_Resistor pull_resistor_8 (.node(pull_resistor_8_node));
  assign pull_resistor_8_node = FSHEN ? FSHI : 1'bz;  // Controlled_Buffer controlled_buffer_17
  and and_4 (Byte_Enable, Byte[0], Byte[1], Byte[2], Byte[3], Byte[4], Byte[5], Byte[6], Byte[7]);
  assign CALL_DATA = and_5_out ? Saved_Addr_q : 16'bz;  // Controlled_Buffer controlled_buffer_18
  and and_5 (and_5_out, CALL, Call_EN);
  Controlled_Buffer #(.width(16)) controlled_buffer_19 (.in(Saved_Addr_q), .en(and_6_out));  // open: out
  buf and_6 (and_6_out, RET);  // AND_Gate
  Decoder #(.enable("false"), .select(3)) decoder_1 (
    .out0(decoder_1_out0), .out1(decoder_1_out1), .sel(INST_q[15:13]));  // open: out2, out3, out4, out5, out6, out7
  or or_24 (ADD, decoder_2_out2, decoder_2_out3);
  or or_25 (SUB, decoder_2_out4, decoder_2_out5);
  Decoder #(.select(5)) decoder_2 (
    .out1(CLR), .out2(decoder_2_out2), .out3(decoder_2_out3), .out4(decoder_2_out4), .out5(decoder_2_out5),
    .out6(SMUL), .out7(MUL), .out8(SDIV), .out9(DIV), .out10(SREM), .out11(UREM), .out12(NEG), .out13(LAND),
    .out14(LOR), .out15(LXOR), .out16(LNOT), .out17(COM), .out18(SFTL), .out19(SFTR), .out20(SFTA),
    .out21(ROTL), .out22(ROTR), .out23(INC), .out24(DEC), .out25(Jmp_t), .out26(JpL), .out27(JpE),
    .out28(JpM), .out29(JpO), .out30(JpN), .out31(JpME), .sel(INST_q[12:8]), .en(decoder_1_out0));  // open: out0
  or or_26 (ALU_Enable, SCOM, DEC, INC, ROTR, ROTL, SFTA, SFTR, SFTL, COM, LNOT, LXOR, LOR, LAND, NEG, UREM, SREM, DIV, SDIV, MUL, SMUL, SUB, ADD);
  nor nor_3 (nor_3_out, COM, SCOM);
  or or_27 (or_27_out, INp, RD);
  Pull_Resistor pull_resistor_9 (.node(pull_resistor_9_node));
  assign pull_resistor_9_node = WR_EN_t ? or_27_out : 1'bz;  // Controlled_Buffer controlled_buffer_20
  assign controlled_buffer_21_out = nor_3_out ? ALU_Enable : 1'bz;  // Controlled_Buffer controlled_buffer_21
  Pull_Resistor pull_resistor_10 (.node(controlled_buffer_21_out));
  assign ALU_opCode = ROTR ? 5'b01110 : 5'bz;  // Controlled_Buffer controlled_buffer_22
  assign ALU_opCode = INC ? 5'b01111 : 5'bz;  // Controlled_Buffer controlled_buffer_23
  assign ALU_opCode = DEC ? 5'b10000 : 5'bz;  // Controlled_Buffer controlled_buffer_24
  assign ALU_opCode = SCOM ? 5'b10100 : 5'bz;  // Controlled_Buffer controlled_buffer_25
  or or_28 (REG_Write, controlled_buffer_21_out, pull_resistor_9_node, RG_RGMOV, RDPG, RDP);
  or or_29 (Data_BusEN, pull_resistor_9_node, RDP);
  Decoder #(.select(5)) decoder_3 (
    .out0(JpLE), .out1(JpNO), .out2(JpI), .out3(FSHI), .out4(HLT), .out5(RD), .out6(WR), .out7(TRAM),
    .out8(RG_RGMOV), .out9(decoder_3_out9), .out10(decoder_3_out10), .out11(decoder_3_out11),
    .out12(decoder_3_out12), .out13(decoder_3_out13), .out14(decoder_3_out14), .out15(SCOM),
    .out16(decoder_3_out16), .out17(decoder_3_out17), .out18(LDSP), .out19(PUSH), .out20(POP), .out21(RDPG),
    .out22(INp), .out23(OUTp), .out24(Set), .out25(LDIH), .out26(LDSB), .out27(WRP), .out28(RDP),
    .out29(CALL), .out30(RET), .sel(INST_q[12:8]), .en(decoder_1_out1));  // open: out31
  assign ALU_opCode = SFTL ? 5'b01010 : 5'bz;  // Controlled_Buffer controlled_buffer_26
  assign ALU_opCode = SFTR ? 5'b01011 : 5'bz;  // Controlled_Buffer controlled_buffer_27
  assign ALU_opCode = SFTA ? 5'b01100 : 5'bz;  // Controlled_Buffer controlled_buffer_28
  assign ALU_opCode = ROTL ? 5'b01101 : 5'bz;  // Controlled_Buffer controlled_buffer_29
  assign ALU_opCode = LOR ? 5'b00101 : 5'bz;  // Controlled_Buffer controlled_buffer_30
  assign ALU_opCode = LXOR ? 5'b00110 : 5'bz;  // Controlled_Buffer controlled_buffer_31
  assign ALU_opCode = LNOT ? 5'b01001 : 5'bz;  // Controlled_Buffer controlled_buffer_32
  assign ALU_opCode = COM ? 5'b10011 : 5'bz;  // Controlled_Buffer controlled_buffer_33
  assign ALU_opCode = SREM ? 5'b10101 : 5'bz;  // Controlled_Buffer controlled_buffer_34
  assign ALU_opCode = UREM ? 5'b00111 : 5'bz;  // Controlled_Buffer controlled_buffer_35
  assign ALU_opCode = NEG ? 5'b01000 : 5'bz;  // Controlled_Buffer controlled_buffer_36
  assign ALU_opCode = LAND ? 5'b00100 : 5'bz;  // Controlled_Buffer controlled_buffer_37
  assign ALU_opCode = SMUL ? 5'b10001 : 5'bz;  // Controlled_Buffer controlled_buffer_38
  assign ALU_opCode = MUL ? 5'b00010 : 5'bz;  // Controlled_Buffer controlled_buffer_39
  assign ALU_opCode = SDIV ? 5'b10010 : 5'bz;  // Controlled_Buffer controlled_buffer_40
  assign ALU_opCode = DIV ? 5'b00011 : 5'bz;  // Controlled_Buffer controlled_buffer_41
  assign ALU_opCode = ADD ? {5{1'b0}} : 5'bz;  // Controlled_Buffer controlled_buffer_42
  assign ALU_opCode = SUB ? 5'b00001 : 5'bz;  // Controlled_Buffer controlled_buffer_43
  or or_30 (or_30_out, OUTp, INp);
  and and_7 (and_7_out, CALL, Call_EN);
  or or_31 (or_31_out, WR, OUTp);
  assign controlled_buffer_44_out = WR_EN_t ? or_31_out : 1'bz;  // Controlled_Buffer controlled_buffer_44
  Pull_Resistor pull_resistor_11 (.node(IO));
  assign IO = WR_EN_t ? or_30_out : 1'bz;  // Controlled_Buffer controlled_buffer_45
  Pull_Resistor pull_resistor_12 (.node(controlled_buffer_44_out));
  Pull_Resistor pull_resistor_13 (.node(pull_resistor_13_node));
  assign pull_resistor_13_node = or_32_out ? WR_EN_t : 1'bz;  // Controlled_Buffer controlled_buffer_46
  or or_32 (or_32_out, WR, OUTp);
  or or_33 (RAM_Write, and_7_out, controlled_buffer_44_out, WRP, PUSHorPULL);
  or or_34 (WR_EN, PUSHorPULL, WRP, pull_resistor_13_node);

  // Other names for the same wires on the sheet: IH[15:0] = DT; MOV = RG_RGMOV; PT[15:0] = Pointer
endmodule

module Branch (
  input  [7:0] Flags,
  input  Jump,
  input  NMI,
  input  Jump_Less,
  input  Jump_Equal,
  input  Jump_More,
  input  Jump_Overflow,
  input  Jump_Negative,
  input  Jump_MoreEqu,
  input  Jump_LessEqu,
  input  Jump_Not,
  input  Jump_Int,
  input  INT,
  output Jump_Enable
);

  assign Jump_Enable = Jump ? 1'b1 : 1'bz;  // Controlled_Buffer controlled_buffer_1
  assign Jump_Enable = Jump_Less ? Flags[5] : 1'bz;  // Controlled_Buffer controlled_buffer_2
  assign Jump_Enable = Jump_Equal ? Flags[4] : 1'bz;  // Controlled_Buffer controlled_buffer_3
  assign Jump_Enable = Jump_More ? Flags[3] : 1'bz;  // Controlled_Buffer controlled_buffer_4
  assign Jump_Enable = Jump_Overflow ? Flags[7] : 1'bz;  // Controlled_Buffer controlled_buffer_5
  assign Jump_Enable = Jump_Negative ? Flags[6] : 1'bz;  // Controlled_Buffer controlled_buffer_6
  assign Jump_Enable = Jump_MoreEqu ? Flags[2] : 1'bz;  // Controlled_Buffer controlled_buffer_7
  assign Jump_Enable = Jump_LessEqu ? Flags[1] : 1'bz;  // Controlled_Buffer controlled_buffer_8
  assign Jump_Enable = Jump_Not ? Flags[0] : 1'bz;  // Controlled_Buffer controlled_buffer_9
  assign Jump_Enable = Jump_Int ? NMI : 1'bz;  // Controlled_Buffer controlled_buffer_10
  Pull_Resistor pull_resistor_1 (.node(Jump_Enable));
  assign Jump_Enable = INT ? 1'b1 : 1'bz;  // Controlled_Buffer controlled_buffer_11
endmodule

module Cycle4Timer (
  input  EN,
  input  CLK,
  input  RST,
  output S0,
  output S1,
  output S2,
  output S3
);

  wire or_1_out;
  wire [1:0] counter_1_q;

  Decoder #(.select(2)) decoder_1 (.out0(S0), .out1(S1), .out2(S2), .out3(S3), .sel(counter_1_q));  // open: en
  Counter #(.max('h3), .trigger("falling"), .width(2)) counter_1 (
    .count(EN), .Q(counter_1_q), .clk(CLK), .clr(or_1_out));  // open: load, D, carry, up
  or or_1 (or_1_out, RST, S3);
endmodule

module Stack_Pack (
  input  Stack_Enable,
  input  [15:0] Pointer,
  input  LD_Stack,
  input  Push,
  input  DataType,
  input  LD_Base,
  input  Clock,
  input  Reset,
  output [15:0] Stack_Addr
);

  wire and_1_out, comparator_1_eq, comparator_1_gt, or_1_out, or_2_out;
  wire [15:0] adder_1_out, adder_2_out, controlled_buffer_1_out, multiplexer_1_out, Stack_Base,
       subtractor_1_out, subtractor_2_out;

  assign controlled_buffer_1_out = LD_Stack ? Pointer : 16'bz;  // Controlled_Buffer controlled_buffer_1
  Register #(.width(16)) u_Stack_Base (.D(Pointer), .en(LD_Base), .clk(Clock), .Q(Stack_Base), .clr(Reset));
  Register #(.trigger("falling"), .width(16)) Stack_Pointer (
    .D(controlled_buffer_1_out), .en(or_1_out), .clk(Clock), .Q(Stack_Addr), .clr(Reset));
  or or_1 (or_1_out, and_1_out, LD_Stack);
  and and_1 (and_1_out, Stack_Enable, or_2_out);
  assign controlled_buffer_1_out = and_1_out ? multiplexer_1_out : 16'bz;  // Controlled_Buffer controlled_buffer_2
  Adder #(.width(16)) adder_1 (.a(Stack_Addr), .b(16'h2), .out(adder_1_out));  // open: cin, cout
  Subtractor #(.width(16)) subtractor_1 (.a(Stack_Addr), .b(16'h2), .out(subtractor_1_out));  // open: bin, bout
  Adder #(.width(16)) adder_2 (.a(Stack_Addr), .b(16'h1), .out(adder_2_out));  // open: cin, cout
  Subtractor #(.width(16)) subtractor_2 (.a(Stack_Addr), .b(16'h1), .out(subtractor_2_out));  // open: bin, bout
  Multiplexer #(.select(2), .width(16)) multiplexer_1 (
    .in0(adder_1_out), .in1(subtractor_1_out), .in2(adder_2_out), .in3(subtractor_2_out),
    .out(multiplexer_1_out), .sel({DataType, Push}));
  Comparator #(.mode("unsigned"), .width(16)) comparator_1 (
    .a(Stack_Base), .b(Stack_Addr), .gt(comparator_1_gt), .eq(comparator_1_eq));  // open: lt
  or or_2 (or_2_out, comparator_1_gt, comparator_1_eq);
endmodule

module RAM_32k (
  input  IO_EN,
  input  EN,
  input  [15:0] ADDR,
  input  Write,
  input  DT_EN,
  input  CLK,
  input  [15:0] Data_IN,
  output [15:0] Data_Out
);

  wire and_2_out, not_1_out, ram_1_p2, ram_1_p3, RAM_EN;
  wire [7:0] controlled_buffer_3_out, controlled_buffer_3_out_2;

  not not_1 (not_1_out, Write);
  and and_1 (RAM_EN, ~IO_EN, EN);  // AND_Gate
  // RAM #(.addrWidth(15), .databus("bidir"), .enables("line"), .line("dual"), .misaligned("true"), .trigger("falling")) ram_1: pin names not known; wires that end beside it: ADDR[14:0], ram_1_p2, ram_1_p3, 1'b1, DT_EN, CLK
  Pull_Resistor pull_resistor_1 (.node(ram_1_p2));
  assign ram_1_p2 = RAM_EN ? Write : 1'bz;  // Controlled_Buffer controlled_buffer_1
  Pull_Resistor pull_resistor_2 (.node(ram_1_p3));
  assign ram_1_p3 = RAM_EN ? not_1_out : 1'bz;  // Controlled_Buffer controlled_buffer_2
  and and_2 (and_2_out, ~Write, RAM_EN);  // AND_Gate
  assign {controlled_buffer_3_out_2, controlled_buffer_3_out} = Write ? Data_IN : 16'bz;  // Controlled_Buffer controlled_buffer_3
  assign Data_Out = and_2_out ? {controlled_buffer_3_out_2, controlled_buffer_3_out} : 16'bz;  // Controlled_Buffer controlled_buffer_4

  // Other names for the same wires on the sheet: WR = Write

  // Notes on the sheet:
  //   Data_IN: pull=down
endmodule

module IO_interface (
  input  IO_EN,
  input  [15:0] ADDR,
  output P_1,
  output P_2,
  output P_3,
  output P_4
);

  wire and_1_out, and_2_out, and_3_out, and_4_out;

  Pull_Resistor pull_resistor_1 (.node(P_1));
  assign P_1 = IO_EN ? and_1_out : 1'bz;  // Controlled_Buffer controlled_buffer_1
  and and_1 (and_1_out, ~ADDR[15], ~ADDR[14], ~ADDR[13], ~ADDR[12], ~ADDR[11], ~ADDR[10], ~ADDR[9], ~ADDR[8], ~ADDR[7], ~ADDR[6], ~ADDR[5], ~ADDR[4], ~ADDR[3], ~ADDR[2], ~ADDR[1], ~ADDR[0]);  // AND_Gate
  Pull_Resistor pull_resistor_2 (.node(P_2));
  assign P_2 = IO_EN ? and_2_out : 1'bz;  // Controlled_Buffer controlled_buffer_2
  and and_2 (and_2_out, ~ADDR[15], ~ADDR[14], ~ADDR[13], ~ADDR[12], ~ADDR[11], ~ADDR[10], ~ADDR[9], ~ADDR[8], ~ADDR[7], ~ADDR[6], ~ADDR[5], ~ADDR[4], ~ADDR[3], ~ADDR[2], ~ADDR[1], ADDR[0]);  // AND_Gate
  Pull_Resistor pull_resistor_3 (.node(P_3));
  assign P_3 = IO_EN ? and_3_out : 1'bz;  // Controlled_Buffer controlled_buffer_3
  and and_3 (and_3_out, ~ADDR[15], ~ADDR[14], ~ADDR[13], ~ADDR[12], ~ADDR[11], ~ADDR[10], ~ADDR[9], ~ADDR[8], ~ADDR[7], ~ADDR[6], ~ADDR[5], ~ADDR[4], ~ADDR[3], ~ADDR[2], ADDR[1], ~ADDR[0]);  // AND_Gate
  Pull_Resistor pull_resistor_4 (.node(P_4));
  assign P_4 = IO_EN ? and_4_out : 1'bz;  // Controlled_Buffer controlled_buffer_4
  and and_4 (and_4_out, ~ADDR[15], ~ADDR[14], ~ADDR[13], ~ADDR[12], ~ADDR[11], ~ADDR[10], ~ADDR[9], ~ADDR[8], ~ADDR[7], ~ADDR[6], ~ADDR[5], ~ADDR[4], ~ADDR[3], ~ADDR[2], ADDR[1], ADDR[0]);  // AND_Gate
endmodule

module Interupt_Request (
  input  IRQ_4,
  input  IRQ_3,
  input  IRQ_2,
  input  IRQ_1,
  input  Clock,
  output INT,
  output NMI
);

  wire controlled_buffer_1_out, controlled_buffer_2_out, d_ff_1_qn, d_ff_2_qn;

  or or_1 (NMI, IRQ_3, IRQ_4);
  D_Flip_Flop #(.trigger("falling")) d_ff_1 (.D(IRQ_1), .clk(Clock), .Qn(d_ff_1_qn));  // open: Q, preset, reset
  D_Flip_Flop #(.trigger("falling")) d_ff_2 (.D(IRQ_2), .clk(Clock), .Qn(d_ff_2_qn));  // open: Q, preset, reset
  assign controlled_buffer_1_out = d_ff_1_qn ? IRQ_1 : 1'bz;  // Controlled_Buffer controlled_buffer_1
  assign controlled_buffer_2_out = d_ff_2_qn ? IRQ_2 : 1'bz;  // Controlled_Buffer controlled_buffer_2
  Pull_Resistor pull_resistor_1 (.node(controlled_buffer_1_out));
  Pull_Resistor pull_resistor_2 (.node(controlled_buffer_2_out));
  or or_2 (INT, controlled_buffer_1_out, controlled_buffer_2_out);
endmodule

module ASCII_HEX (
  input  [7:0] A_IN,
  output [3:0] B_OUT
);

  PLA #(.in_width(8), .out_width(4), .\table ("00110000 0000 # 0\n00110001 0001 # 1\n00110010 0010 # 2\n00110011 0011 # 3\n00110100 0100 # 4\n00110101 0101 # 5\n00110110 0110 # 6\n00110111 0111 # 7\n00111000 1000 # 8\n00111001 1001 # 9\n01x00001 1010 # A\n01x00010 1011 # B\n01x00011 1100 # C\n01x00100 1101 # D\n01x00101 1110 # E\n01x00110 1110 # F")) pla_1 (
    .in(A_IN), .out(B_OUT));
endmodule

module MMAP (
  input  [15:0] ADDR,
  output EN_1,
  output EN_2,
  output [15:0] ADDR_OUT,
  output EN_3,
  output EN_4
);

  wire comparator_1_eq, comparator_1_gt, comparator_1_lt, comparator_2_eq, comparator_2_gt, comparator_2_lt,
       comparator_3_eq, comparator_3_gt, comparator_3_lt, comparator_4_eq, comparator_4_gt, or_2_out,
       or_3_out, or_4_out;
  wire [15:0] subtractor_1_out, subtractor_2_out, subtractor_3_out;

  Comparator #(.mode("unsigned"), .width(16)) comparator_1 (
    .a(16'h3fff), .b(ADDR), .gt(comparator_1_gt), .eq(comparator_1_eq), .lt(comparator_1_lt));
  Comparator #(.mode("unsigned"), .width(16)) comparator_2 (
    .a(16'hbfff), .b(ADDR), .gt(comparator_2_gt), .eq(comparator_2_eq), .lt(comparator_2_lt));
  Subtractor #(.width(16)) subtractor_1 (.a(ADDR), .b(16'h4000), .out(subtractor_1_out));  // open: bin, bout
  Comparator #(.mode("unsigned"), .width(16)) comparator_3 (
    .a(16'hc7ff), .b(ADDR), .gt(comparator_3_gt), .eq(comparator_3_eq), .lt(comparator_3_lt));
  Subtractor #(.width(16)) subtractor_2 (.a(ADDR), .b(16'hc000), .out(subtractor_2_out));  // open: bin, bout
  Comparator #(.mode("unsigned"), .width(16)) comparator_4 (
    .a(16'hd7ff), .b(ADDR), .gt(comparator_4_gt), .eq(comparator_4_eq));  // open: lt
  Subtractor #(.width(16)) subtractor_3 (.a(ADDR), .b(16'hc800), .out(subtractor_3_out));  // open: bin, bout
  or or_1 (EN_1, comparator_1_gt, comparator_1_eq);
  and and_1 (EN_2, comparator_1_lt, or_2_out);
  or or_2 (or_2_out, comparator_2_gt, comparator_2_eq);
  and and_2 (EN_3, comparator_2_lt, or_3_out);
  or or_3 (or_3_out, comparator_3_gt, comparator_3_eq);
  and and_3 (EN_4, comparator_3_lt, or_4_out);
  or or_4 (or_4_out, comparator_4_gt, comparator_4_eq);
  assign ADDR_OUT = EN_1 ? ADDR : 16'bz;  // Controlled_Buffer controlled_buffer_1
  assign ADDR_OUT = EN_2 ? subtractor_1_out : 16'bz;  // Controlled_Buffer controlled_buffer_2
  assign ADDR_OUT = EN_3 ? subtractor_2_out : 16'bz;  // Controlled_Buffer controlled_buffer_3
  assign ADDR_OUT = EN_4 ? subtractor_3_out : 16'bz;  // Controlled_Buffer controlled_buffer_4
endmodule

module ROM_16k (
  input  [15:0] ADDR,
  input  OUT_EN,
  output [15:0] Data_Out
);

  wire [7:0] rom_1_p2, rom_1_p3;

  // ROM #(.addrWidth(14), .line("dual"), .misaligned("true")) rom_1: pin names not known; wires that end beside it: ADDR[13:0], rom_1_p2, rom_1_p3
  assign Data_Out = OUT_EN ? {rom_1_p2, rom_1_p3} : 16'bz;  // Controlled_Buffer controlled_buffer_1

  // Notes on the sheet:
  //   contents of rom_1 (hex, n*v repeats v):
  //   25 0 0 4 b7 fe 3a 0 32 0 3d 0 3 e4 984*0 25 0 3 ea 0 41 37 0 0 0 3e
endmodule

module RAM_2k (
  input  IO_EN,
  input  EN,
  input  [15:0] ADDR,
  input  Write,
  input  DT_EN,
  input  CLK,
  input  [15:0] Data_IN,
  output [15:0] Data_Out
);

  wire and_2_out, not_1_out, ram_1_p2, ram_1_p3, RAM_EN;
  wire [7:0] controlled_buffer_3_out, controlled_buffer_3_out_2;

  not not_1 (not_1_out, Write);
  and and_1 (RAM_EN, ~IO_EN, EN);  // AND_Gate
  // RAM #(.addrWidth(11), .databus("bidir"), .enables("line"), .line("dual"), .misaligned("true"), .trigger("falling")) ram_1: pin names not known; wires that end beside it: ADDR[10:0], ram_1_p2, ram_1_p3, 1'b1, DT_EN, CLK
  Pull_Resistor pull_resistor_1 (.node(ram_1_p2));
  assign ram_1_p2 = RAM_EN ? Write : 1'bz;  // Controlled_Buffer controlled_buffer_1
  Pull_Resistor pull_resistor_2 (.node(ram_1_p3));
  assign ram_1_p3 = RAM_EN ? not_1_out : 1'bz;  // Controlled_Buffer controlled_buffer_2
  and and_2 (and_2_out, ~Write, RAM_EN);  // AND_Gate
  assign {controlled_buffer_3_out_2, controlled_buffer_3_out} = Write ? Data_IN : 16'bz;  // Controlled_Buffer controlled_buffer_3
  assign Data_Out = and_2_out ? {controlled_buffer_3_out_2, controlled_buffer_3_out} : 16'bz;  // Controlled_Buffer controlled_buffer_4

  // Other names for the same wires on the sheet: WR = Write

  // Notes on the sheet:
  //   Data_IN: pull=down
endmodule

module ROM_4k (
  input  [15:0] ADDR,
  input  OUT_EN,
  output [15:0] Data_Out
);

  wire [7:0] rom_1_p2, rom_1_p3;

  // ROM #(.addrWidth(12), .line("dual"), .misaligned("true")) rom_1: pin names not known; wires that end beside it: ADDR[11:0], rom_1_p2, rom_1_p3
  assign Data_Out = OUT_EN ? {rom_1_p2, rom_1_p3} : 16'bz;  // Controlled_Buffer controlled_buffer_1
endmodule
